# Fritzing sketch Montage (saved by Fritzing 0.9.3b)

parts:
  Part1 = Adafruit Feather HUZZAH ESP8266 [part_number="Adafruit #2821"]
  Composant1 = RFID-RC522-v3

nets:
  GND: Part1.GND, Composant1.GND
  3.3V: Part1.3.3V, Composant1.3.3V
  N1: Part1.GPIO14/SCK, Composant1.SCK
  N2: Part1.GPIO12/MISO, Composant1.MISO
  N3: Part1.GPIO13/MOSI, Composant1.MOSI
  N4: Part1.GPIO5/SCL, Composant1.SDA
  N5: Part1.GPIO4/SDA, Composant1.RST

custom parts:
  Adafruit Feather HUZZAH ESP8266: his is the Adafruit Feather HUZZAH ESP8266 - our take on an 'all-in-one' ESP8266 WiFi development board with built in USB and battery charging. Its an ESP8266 WiFi module with all the extras you need, ready to rock! We have other boards in the Feather family, check'em out here. At the Feather HUZZAH's heart is an ESP8266 WiFi microcontroller clocked at 80 MHz and at 3.3V logic. This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
  RFID-RC522-v3: A simple China made RFID-RC522 Reader (6x4 cm); do check the pin labels, as this is a MFRC522 based clone.
